# Fritzing sketch Proyecto_Interfaces_esquematico (saved by Fritzing 0.9.3b)
breadboards: 2

parts:
  U1 = NodeMCU V1.0
  DHT1 = DHT11 Humitidy and Temperature Sensor
  Componente1 = FC-28 Soil Hygrometer Module - Probe
  U2 = POT [package=pot_mammoth]
  U3 = LCD-16X2 [package=lcd-16x2_noholes]
  LCM1602_IIC1 = LCM1602 IIC [part_number="LCM1602 IIC" chip_label="LCM1602 IIC" package="DIP (Dual Inline) [THT]"]
  S1 = Momentary Switch [package=ksa_sealed_tac_switch]
  R1 = Resistor [tolerance=±5% resistance=220 package=THT]

nets:
  N1: U1.D1, LCM1602_IIC1.SCL
  N2: U1.D2, LCM1602_IIC1.SDA
  N3: DHT1.VDD, Componente1.NEG
  N4: DHT1.GND, U2.A
  N5: Componente1.POS, U2.S
  VSS: U3.VSS, LCM1602_IIC1.VSS
  VDD: U3.VDD, LCM1602_IIC1.VDD
  N6: U3.VO, LCM1602_IIC1.V0
  N7: U3.RS, LCM1602_IIC1.RS
  N8: U3.R_W, LCM1602_IIC1.RW
  N9: U3.E, LCM1602_IIC1.E
  N10: U3.DB0, LCM1602_IIC1.D0
  N11: U3.DB1, LCM1602_IIC1.D1
  N12: U3.DB2, LCM1602_IIC1.D2
  N13: U3.DB3, LCM1602_IIC1.D3
  N14: U3.DB4, LCM1602_IIC1.D4
  N15: U3.DB5, LCM1602_IIC1.D5
  N16: U3.DB6, LCM1602_IIC1.D6
  N17: U3.DB7, LCM1602_IIC1.D7
  N18: U3.A, LCM1602_IIC1.A
  N19: U3.K, LCM1602_IIC1.K
  N20: S1.4, R1.Pin_1

custom parts:
  NodeMCU V1.0: ESP8266 based NodeMCU
  DHT11 Humitidy and Temperature Sensor: DHT11 Humidity and Temperature Sensor
  FC-28 Soil Hygrometer Module - Probe: The FC-28 is a soil hygrometer module that uses the Texas Instruments LM393 comparator chip to provide an analog measurement of soil humidity.
  LCM1602 IIC: I2C-Module to use a 1602 or 2004 LCD on with the wire.h libory Serial LCD Modul
